// Logisim project ex1.circ as structural Verilog: 1 circuit, main circuit generate_immediate
module generate_immediate (
  input  [31:0] INSTRUCTION,
  output [31:0] IMMEDIATE
);

  wire [10:0] adder_1_out, bit_extender_1_out, bit_extender_2_out, shifter_1_out;

  assign bit_extender_1_out = {{4{1'b0}}, INSTRUCTION[31:25]};  // Bit_Extender bit_extender_1
  assign bit_extender_2_out = {{6{1'b0}}, INSTRUCTION[11:7]};  // Bit_Extender bit_extender_2
  Shifter #(.width(11)) shifter_1 (.in(bit_extender_1_out), .\dist (4'b0101), .out(shifter_1_out));
  Adder #(.width(11)) adder_1 (.a(shifter_1_out), .b(bit_extender_2_out), .out(adder_1_out));  // open: cin, cout
  assign IMMEDIATE = {{21{INSTRUCTION[31]}}, adder_1_out};  // Bit_Extender bit_extender_3
endmodule
